# Fritzing sketch bats (saved by Fritzing 0.9.3b)
breadboards: 1

parts:
  Part1 = Arduino Uno (Rev3)
  R2 = Photocell (LDR) [package=THT]
  R3 = Resistor [tolerance=±5% resistance=10k package="0402 [SMD]"]
  J1 = Basic Servo
  J2 = Basic Servo

nets:
  N1: Part1.A0, R2.pin_1, R3.Pin_1
  N2: Part1.D9_PWM, J2.pulse
  N3: Part1.D10_PWM/SS, J1.pulse
  VCC: Part1.5V, R2.pin_0, J1.vcc, J2.vcc
  GND: Part1.GND, R3.Pin_0, J1.gnd, J2.gnd
