# Fritzing sketch edited_marquee (saved by Fritzing 0.9.3b)
breadboards: 1

parts:
  Part1 = Arduino Uno (Rev3)
  LED1 = LED - 5mm [color="Yellow (585nm)" package="5 mm [THT]"]
  LED2 = LED - 5mm [color="Yellow (585nm)" package="5 mm [THT]"]
  LED3 = LED - 5mm [color="Yellow (585nm)" package="5 mm [THT]"]
  LED4 = LED - 5mm [color="Yellow (585nm)" package="5 mm [THT]"]
  LED5 = LED - 5mm [color="Yellow (585nm)" package="5 mm [THT]"]
  LED6 = LED - 5mm [color="Yellow (585nm)" package="5 mm [THT]"]
  LED7 = LED - 5mm [color="Yellow (585nm)" package="5 mm [THT]"]
  R1 = Resistor [tolerance=±5% resistance=220 package=THT]
  R2 = Resistor [tolerance=±5% resistance=220 package=THT]
  R3 = Resistor [tolerance=±5% resistance=220 package=THT]
  R4 = Resistor [tolerance=±5% resistance=220 package=THT]
  R5 = Resistor [tolerance=±5% resistance=220 package=THT]
  R6 = Resistor [tolerance=±5% resistance=220 package=THT]
  R7 = Resistor [tolerance=±5% resistance=220 package=THT]

nets:
  N1: Part1.GND, LED1.cathode, LED2.cathode, LED3.cathode, LED4.cathode, LED5.cathode, LED6.cathode, LED7.cathode
  N2: Part1.D0/RX, R1.Pin_0
  N3: Part1.D1/TX, R2.Pin_0
  N4: Part1.D2, R3.Pin_0
  N5: Part1.D3_PWM, R4.Pin_0
  N6: Part1.D4, R5.Pin_0
  N7: Part1.D5_PWM, R6.Pin_0
  N8: Part1.D6_PWM, R7.Pin_0
  N9: LED1.anode, R1.Pin_1
  N10: LED2.anode, R5.Pin_1
  N11: LED3.anode, R6.Pin_1
  N12: LED4.anode, R7.Pin_1
  N13: LED5.anode, R4.Pin_1
  N14: LED6.anode, R3.Pin_1
  N15: LED7.anode, R2.Pin_1
